# Fritzing sketch R03_N1 (saved by Fritzing 0.9.6b)
breadboards: 1

parts:
  Componente4 = Arduino Uno (Rev3)
  MPX4250AP1 = MPX4250AP pressure sensor [part_number=MPX]

nets:
  N1: Componente4.A0, MPX4250AP1.V_out
  N2: Componente4.5V, MPX4250AP1.Vs
  GND: Componente4.GND, MPX4250AP1.GND
